# Fritzing sketch 11_Two-DCmotors (saved by Fritzing 0.8.7b)
breadboards: 1

parts:
  IC1 = L293D [package=THT]
  U1 = attiny85 [package=dip]
  M1 = DC Motor
  VCC2 = 4 x AAA Battery Mount
  M2 = DC Motor
  VCC3 = Battery block 9V

nets:
  N1: IC1.Enable_1, U1.Pin_5
  N2: IC1.In_1, U1.Pin_7
  N3: IC1.Out_1_(_Controlled_by_Enable_1_), M2.pin_1
  N4: IC1.0V, U1.Pin_4, VCC2.+, VCC3.-
  N5: IC1.Out_2_(_Controlled_by_Enable_1_), M2.pin_2
  N6: IC1.In_2, U1.Pin_2
  N7: IC1.+Vmotor, VCC3.+
  N8: IC1.Enable_2, U1.Pin_6
  N9: IC1.In_3, U1.Pin_3
  N10: IC1.Out_3_(_Controlled_by_Enable_2_), M1.pin_2
  N11: IC1.Out_4_(_Controlled_by_Enable_2_), M1.pin_1
  N12: IC1.In_4, U1.Pin_1
  N13: IC1.+V, U1.Pin_8, VCC2.-

custom parts:
  4 x AAA Battery Mount: A 4 x AAA battery pack (4.8 Volts with recharables)
