# Fritzing sketch Twisting-potentiometer (saved by Fritzing 0.8.7b)
breadboards: 1

parts:
  U1 = attiny85 [package=dip]
  U2 = POT [package=pot_mammoth]
  LED1 = LED - 5mm [color="Red (633nm)" package="5 mm [THT]"]
  V1 = DC Power [voltage=5]
  R1 = Resistor [tolerance=±5% resistance=220 package=THT]

nets:
  N1: U1.Pin_3, U2.S
  N2: U1.Pin_4, U2.E, LED1.cathode, V1.V-
  N3: U1.Pin_6, R1.Pin_1
  N4: U1.Pin_8, U2.A, V1.V+
